// Logisim project trabalho PCL.circ as structural Verilog
module somador_simples (
  input  A,
  input  B,
  output S,
  output Co
);

  xor xor_1 (S, A, B);
  and and_1 (Co, A, B);
endmodule

module somador_1_bit (
  input  A,
  input  B,
  input  Te,
  output S,
  output Ts
);

  wire and_1_out, and_2_out, and_3_out;

  // XOR_Gate xor_1 has open pins: in1=A, in3=B, out=open
  and and_1 (and_1_out, Te, B);
  and and_2 (and_2_out, A, Te);
  and and_3 (and_3_out, B, Te);
  ExactlyOne xor_2 (.out(Ts), .in0(and_1_out), .in2(and_2_out), .in4(and_3_out));
  buf xor_3 (S, Te);  // XOR_Gate
endmodule

module somador___subtrator_7_bits (
  input  S_S,
  input  [6:0] A,
  input  [6:0] B,
  output [6:0] R,
  output Sinal,
  output OF
);

  wire somador_1_bit_1_ts, somador_1_bit_2_ts, somador_1_bit_3_ts, somador_1_bit_4_ts, somador_1_bit_5_ts,
       somador_1_bit_6_ts, somador_1_bit_7_ts, xor_1_out, xor_2_out, xor_3_out, xor_4_out, xor_5_out,
       xor_6_out, xor_7_out;

  buf xor_1 (xor_1_out, B[0]);  // XOR_Gate
  buf xor_2 (xor_2_out, B[1]);  // XOR_Gate
  buf xor_3 (xor_3_out, B[2]);  // XOR_Gate
  buf xor_4 (xor_4_out, B[3]);  // XOR_Gate
  buf xor_5 (xor_5_out, B[4]);  // XOR_Gate
  buf xor_6 (xor_6_out, B[5]);  // XOR_Gate
  xor xor_7 (xor_7_out, S_S, B[6]);
  somador_1_bit somador_1_bit_1 (.A(A[0]), .B(xor_1_out), .Te(S_S), .S(R[0]), .Ts(somador_1_bit_1_ts));
  somador_1_bit somador_1_bit_2 (.A(A[1]), .B(xor_2_out), .Te(somador_1_bit_1_ts), .S(R[1]), .Ts(somador_1_bit_2_ts));
  somador_1_bit somador_1_bit_3 (.A(A[2]), .B(xor_3_out), .Te(somador_1_bit_2_ts), .S(R[2]), .Ts(somador_1_bit_3_ts));
  somador_1_bit somador_1_bit_4 (.A(A[3]), .B(xor_4_out), .Te(somador_1_bit_3_ts), .S(R[3]), .Ts(somador_1_bit_4_ts));
  somador_1_bit somador_1_bit_5 (.A(A[4]), .B(xor_5_out), .Te(somador_1_bit_4_ts), .S(R[4]), .Ts(somador_1_bit_5_ts));
  somador_1_bit somador_1_bit_6 (.A(A[5]), .B(xor_6_out), .Te(somador_1_bit_5_ts), .S(R[5]), .Ts(somador_1_bit_6_ts));
  somador_1_bit somador_1_bit_7 (.A(A[6]), .B(xor_7_out), .Te(somador_1_bit_6_ts), .S(R[6]), .Ts(somador_1_bit_7_ts));
  xor xor_8 (OF, somador_1_bit_7_ts, somador_1_bit_6_ts);

  assign Sinal = R[6];
endmodule

module Complemento_de_2 (
  input  C2,
  input  [6:0] N,
  output [6:0] R
);

  wire [6:0] xor_1_out;

  xor xor_1 (xor_1_out[0], N[0], C2);
  xor xor_2 (xor_1_out[1], N[1], C2);
  xor xor_3 (xor_1_out[2], N[2], C2);
  xor xor_4 (xor_1_out[3], N[3], C2);
  xor xor_5 (xor_1_out[4], N[4], C2);
  xor xor_6 (xor_1_out[5], N[5], C2);
  xor xor_7 (xor_1_out[6], N[6], C2);
  somador___subtrator_7_bits somador_subtrator_7_bits_1 (
    .S_S(1'b0), .A(xor_1_out), .B({{6{1'b0}}, C2}), .R(R));  // open: Sinal, OF
endmodule

module Somador___subtrator_C2 (
  input  S_S,
  input  SINAL_A,
  input  SINAL_B,
  input  [6:0] A,
  input  [6:0] B,
  output [6:0] R,
  output OF,
  output SINAL
);

  wire [6:0] complemento_de_2_1_r, complemento_de_2_2_r, somador_subtrator_7_bits_1_r;

  Complemento_de_2 complemento_de_2_1 (.C2(SINAL_A), .N(A), .R(complemento_de_2_1_r));
  Complemento_de_2 complemento_de_2_2 (.C2(SINAL_B), .N(B), .R(complemento_de_2_2_r));
  somador___subtrator_7_bits somador_subtrator_7_bits_1 (
    .S_S(S_S), .A(complemento_de_2_1_r), .B(complemento_de_2_2_r), .Sinal(SINAL), .OF(OF),
    .R(somador_subtrator_7_bits_1_r));
  Complemento_de_2 complemento_de_2_3 (.C2(SINAL), .N(somador_subtrator_7_bits_1_r), .R(R));

  // Other names for the same wires on the sheet: _2 = SINAL_B
endmodule
